# Fritzing sketch C.E.W.B. Circuit Diagram (saved by Fritzing 1.0.6)
breadboards: 1

parts:
  Microprocessor = Arduino Uno (Rev3)
  Motor = DC Motor [voltage_(max)=24V voltage_(min)=3V]
  DRV8871_Motor_Driver = IC, DIP package, 6 pins [chip_label=DRV8871]
  24V = Battery block 24V
  Encoder = IC, DIP package, 4 pins [chip_label=E8P]

nets:
  N1: Microprocessor.D9_PWM, DRV8871_Motor_Driver.pin3
  N2: Microprocessor.D10_PWM/SS, DRV8871_Motor_Driver.pin6
  N3: Microprocessor.GND, DRV8871_Motor_Driver.pin2, 24V.-, Encoder.pin4
  N4: Microprocessor.D5_PWM, Encoder.pin1
  N5: Microprocessor.D6_PWM, Encoder.pin2
  N6: Microprocessor.5V, Encoder.pin3
  N7: Motor.pin_1, DRV8871_Motor_Driver.pin5
  N8: Motor.pin_2, DRV8871_Motor_Driver.pin4
  N9: DRV8871_Motor_Driver.pin1, 24V.+

custom parts:
  Battery block 24V: Your standard 9 Volts battery block
